# Fritzing sketch Mic Amplifier (saved by Fritzing 0.9.3b)
breadboards: 1

parts:
  U1 = LM 358 Dual Op-Amp [part_number=LM358 package="DIP8 [THT]"]
  MIC = Microphone
  C1_6_8uF = Capacitor Polarized [package=cpol-radial-10uf-25v]
  R5 = Resistor [tolerance=±5% resistance=10k package=THT]
  R4 = Resistor [tolerance=±5% resistance=10k package=THT]
  R2 = Resistor [tolerance=±5% resistance=3.3k package=THT]
  R3 = Resistor [tolerance=±5% resistance=680k package=THT]
  R1 = Resistor [tolerance=±5% resistance=2.7k package=THT]
  R6 = Resistor [tolerance=±5% resistance=150k package=THT]
  C2 = Ceramic Capacitor [capacitance=1nF package="100 mil [THT, multilayer]"]
  R7 = Resistor [tolerance=±5% resistance=1.8k package=THT]
  C3 = Ceramic Capacitor [capacitance=100nF package="100 mil [THT, multilayer]"]

nets:
  N1: U1.connector0, R3.Pin_0, C2.0
  N2: U1.connector1, R2.Pin_1, R3.Pin_1
  N3: U1.connector2, R5.Pin_1, R4.Pin_1
  5V: U1.connector7, R4.Pin_0, R1.Pin_0
  GND: MIC.pin1, R5.Pin_0, R6.Pin_0, C3.1
  N4: MIC.pin2, C1_6_8uF.+, C1_6_8uF.-, R2.Pin_0, R1.Pin_1
  N5: R6.Pin_1, C2.1, R7.Pin_0
  Vout: R7.Pin_1, C3.0

notes:
  -5V
  +5V
  GND
