# Fritzing sketch Schmitt Trigger (saved by Fritzing 0.9.3b)

parts:
  U1 = LM 358 Dual Op-Amp [part_number=LM358 package="DIP8 [THT]"]
  R3 = Resistor [tolerance=±5% resistance=10k package=THT]
  R1 = Resistor [tolerance=±5% resistance=10k package=THT]
  R2 = Resistor [tolerance=±5% resistance=10k package=THT]

nets:
  Vout: U1.connector0, R2.Pin_0
  Vin: U1.connector1
  Va: U1.connector2, R3.Pin_1, R1.Pin_0, R2.Pin_1
  N1: U1.connector7, R1.Pin_1
  GND: R3.Pin_0
